# Fritzing sketch PiTUT1 (saved by Fritzing 0.9.8b)
breadboards: 1

parts:
  Mod1 = Raspberry Pi Pico
  Grove1 = TM1637 7segment 4digit display
  S1 = Pushbutton [package="[THT]"]
  Part1 = NeoPixel Stick [part_number=1426]

nets:
  GND: Mod1.pin_3, Mod1.pin_8, Mod1.pin_13, Mod1.pin_18, Mod1.pin_23, Mod1.pin_28, Mod1.pin_33, Mod1.pin_38, Grove1.GND, S1.Pin_3, S1.Pin_4, Part1.GND
  N1: Mod1.pin_20, Part1.DATAIN
  N2: Mod1.pin_21, S1.Pin_1, S1.Pin_2
  N3: Mod1.pin_31, Grove1.CLK
  N4: Mod1.pin_32, Grove1.DIO
  VCC: Mod1.pin_36, Grove1.Vcc, Part1.+5V

custom parts:
  Raspberry Pi Pico: Raspberry Pi Pico. Based around the RP2040 microcontroller the Pico is a low cost microcontroller device bringing Raspberry Pi quality, cost, and easy of use to the microcontroller space. Jan 2021, Split part in to two versions: tht (this one) and SMD. This one will drill holes for a .1 in header in pcb to allow plugging in the module as well as providing pads to solder the module to the top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
  NeoPixel Stick: Make your own little LED strip arrangement with this stick of NeoPixel LEDs. We crammed 8 of the tiny 5050 (5mm x 5mm) smart RGB LEDs onto a PCB with mounting holes and a chainable design. Use only one microcontroller pin to control as many as you can chain together! Each LED is addressable as the driver chip is inside the LED. Each one has ~18mA constant current drive so the color will be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
